# Fritzing sketch photonlab (saved by Fritzing 0.9.2b)
breadboards: 1

parts:
  Part1 = Photon
  R1 = PHOTOCELL [package=photocell]
  R2 = Resistor [tolerance=±5% resistance=10k package=THT]
  LED1 = LED - 5mm [color="Red (633nm)" package="5 mm [THT]"]

nets:
  N1: Part1.A0, R1.P$1, R2.Pin_1
  N2: Part1.GND, R1.P$2, LED1.cathode
  N3: Part1.D1, LED1.anode
  N4: Part1.3V3, R2.Pin_0
